# Fritzing sketch Skutter diagram (saved by Fritzing 0.9.3b)
breadboards: 1

parts:
  WeMos_D1_Mini1 = WeMos D1 Mini  # not connected
  RGB_SMD_LED1 = SMD RGB LED (WS2812) [package=5050]
  R1 = Resistor [tolerance=±5% resistance=560 package="2512 [SMD]"]
  C1 = Capacitor Polarized [package=panasonic_c]
  J1 = Basic Servo
  J2 = Basic Servo
  VCC2 = 4 x AAA Battery Mount

nets:
  GND: RGB_SMD_LED1.DOut, C1.-, J1.gnd, J2.gnd, VCC2.-
  N1: RGB_SMD_LED1.DIn, R1.Pin_1
  VCC: RGB_SMD_LED1.VCC, C1.+, J1.vcc, J2.vcc, VCC2.+
